// Logisim project CPU.circ as structural Verilog: 7 circuits, main circuit main
module main (
  input  RESET
);

  wire clock_1_out, cpu_1_clock_ou, cpu_1_read, cpu_1_wrt;
  wire [15:0] cpu_1_addr, cpu_1_instruction_pointer, cpu_1_op, ram_1_dout, ram_2_dout;

  RAM #(.addrWidth(16), .dataWidth(16), .trigger("falling")) ram_1 (
    .addr(cpu_1_instruction_pointer), .clk(clock_1_out), .dout(ram_1_dout));  // open: we, oe, din
  Clock clock_1 (.out(clock_1_out));
  CPU cpu_1 (
    .INSTRUCTION(ram_1_dout), .Clock(clock_1_out), .Reset(RESET), .IP(ram_2_dout),
    .Instruction_Pointer(cpu_1_instruction_pointer), .ADDR(cpu_1_addr), .WRT(cpu_1_wrt), .READ(cpu_1_read),
    .Clock_OU(cpu_1_clock_ou), .OP(cpu_1_op));
  RAM #(.addrWidth(16), .asyncread("true"), .clearpin("true"), .dataWidth(16)) ram_2 (
    .addr(cpu_1_addr), .we(cpu_1_wrt), .oe(cpu_1_read), .clk(cpu_1_clock_ou), .din(cpu_1_op),
    .dout(ram_2_dout), .clr(RESET));
endmodule

module CPU (
  input  [15:0] INSTRUCTION,
  input  Clock,
  input  Reset,
  input  [15:0] IP,
  output [15:0] Instruction_Pointer,
  output [15:0] ADDR,
  output WRT,
  output READ,
  output Clock_OU,
  output [15:0] OP
);

  wire A1, A2, A3, ADD, AMD, and_4_out, and_5_out, and_6_out, and_7_out, B1, B2, B3, BP1, BP2, BP3,
       buffer_1_out, buffer_2_out, buffer_3_out, buffer_4_out, buffer_5_out, buffer_7_out, buffer_8_out,
       buffering_2_out_2, buffering_3_out_2, C1, C2, C3, CLOCK1, CLOCK2, CLOCK3, CMP,
       controlled_buffer_5_out, controlled_buffer_8_out, cpu_decoder_1_noop, cpu_decoder_1_ou,
       cpu_decoder_1_src_1, cpu_decoder_1_src_2, D1, D2, D3, IMM_EN, INV_VAL, JE, JG, JL, JMP, MOV,
       not_1_out, not_2_out, not_3_out, not_4_out, not_5_out, not_6_out, not_7_out, or_3_out, OW, POP,
       PSHPOP, PUSH, s1, s2, s3, SHL, SHR, SP1, SP2, SP3, SUB, t1, t2, t3, WRT_t, xor_1_out, XOW;
  wire [2:0] comparator_1_gt, controlled_buffer_35_out, register_7_q;
  wire [15:0] adder_1_out, and_1_out, BP_q, controlled_buffer_3_out, controlled_buffer_7_out,
       controlled_buffer_10_out, controlled_buffer_11_out, controlled_buffer_18_out, counter_1_q,
       imm_save_1_out_5, or_1_out, register_1_q, register_2_q, register_3_q, register_4_q, register_5_q,
       register_6_q, subtractor_1_out, subtractor_2_out, xor_2_out;

  Controlled_Buffer #(.width(16)) controlled_buffer_1 ();  // open: in, out, en
  buf buffer_1 (buffer_1_out, Clock);
  buf buffer_2 (buffer_2_out, buffer_1_out);
  buf buffer_3 (buffer_3_out, buffer_2_out);
  buf buffer_4 (buffer_4_out, buffer_3_out);
  buf buffer_5 (buffer_5_out, buffer_4_out);
  buf buffer_6 (CLOCK1, buffer_5_out);
  assign OP = IMM_EN ? INSTRUCTION : 16'bz;  // Controlled_Buffer controlled_buffer_2
  not not_1 (not_1_out, IMM_EN);
  assign {controlled_buffer_3_out[15], INV_VAL, controlled_buffer_3_out[13:0]} = not_1_out ? INSTRUCTION : 16'bz;  // Controlled_Buffer controlled_buffer_3
  assign {controlled_buffer_3_out[15], INV_VAL, controlled_buffer_3_out[13:0]} = IMM_EN ? imm_save_1_out_5 : 16'bz;  // Controlled_Buffer controlled_buffer_4
  IMM_SAVE imm_save_1 (
    .IMM_VAL(controlled_buffer_3_out[15]), .INSTR_IN(INSTRUCTION), .Clock(Clock), .Reset(Reset),
    .out_5(imm_save_1_out_5), .IMM_ENABLE(IMM_EN));
  xor xor_1 (xor_1_out, controlled_buffer_3_out[15], IMM_EN);
  Buffering buffering_1 (.in_1(CLOCK2), .out_2(CLOCK3));
  not not_2 (not_2_out, READ);
  assign controlled_buffer_5_out = not_2_out ? CLOCK2 : 1'bz;  // Controlled_Buffer controlled_buffer_5
  CPU_Decoder cpu_decoder_1 (
    .OPCODE(controlled_buffer_3_out[13:10]), .UNENABLE(xor_1_out), .NOOP(cpu_decoder_1_noop), .MOV(MOV),
    .AMD(AMD), .OW(OW), .XOW(XOW), .ADD(ADD), .SUB(SUB), .SHL(SHL), .SHR(SHR), .CMP(CMP), .JMP(JMP), .JE(JE),
    .JL(JL), .JG(JG), .WRT(WRT_t), .READ(READ), .SRC_1(cpu_decoder_1_src_1), .SRC_2(cpu_decoder_1_src_2),
    .OU(cpu_decoder_1_ou));
  assign controlled_buffer_5_out = READ ? buffering_2_out_2 : 1'bz;  // Controlled_Buffer controlled_buffer_6
  Buffering buffering_2 (.in_1(CLOCK3), .out_2(buffering_2_out_2));
  assign controlled_buffer_7_out = READ ? IP : 16'bz;  // Controlled_Buffer controlled_buffer_7
  not not_3 (not_3_out, READ);
  assign controlled_buffer_8_out = not_4_out ? cpu_decoder_1_src_1 : 1'bz;  // Controlled_Buffer controlled_buffer_8
  not not_4 (not_4_out, IMM_EN);
  assign controlled_buffer_7_out = not_3_out ? controlled_buffer_10_out : 16'bz;  // Controlled_Buffer controlled_buffer_9
  assign controlled_buffer_10_out = not_5_out ? controlled_buffer_11_out : 16'bz;  // Controlled_Buffer controlled_buffer_10
  not not_5 (not_5_out, INV_VAL);
  assign controlled_buffer_10_out = INV_VAL ? ~controlled_buffer_11_out : 16'bz;  // Controlled_Inverter controlled_inverter_1
  Register #(.width(16)) register_1 (
    .D(controlled_buffer_7_out), .en(A1), .clk(controlled_buffer_5_out), .Q(register_1_q), .clr(Reset));
  Register #(.width(16)) register_2 (
    .D(controlled_buffer_7_out), .en(B1), .clk(controlled_buffer_5_out), .Q(register_2_q), .clr(Reset));
  Register #(.width(16)) register_3 (
    .D(controlled_buffer_7_out), .en(C1), .clk(controlled_buffer_5_out), .Q(register_3_q), .clr(Reset));
  Register #(.width(16)) register_4 (
    .D(controlled_buffer_7_out), .en(D1), .clk(controlled_buffer_5_out), .Q(register_4_q), .clr(Reset));
  Register #(.width(16)) register_5 (
    .D(controlled_buffer_7_out), .en(s1), .clk(controlled_buffer_5_out), .Q(register_5_q), .clr(Reset));
  Register #(.width(16)) register_6 (
    .D(controlled_buffer_7_out), .en(t1), .clk(controlled_buffer_5_out), .Q(register_6_q), .clr(Reset));
  Register #(.width(16)) BP (
    .D(controlled_buffer_7_out), .en(BP1), .clk(controlled_buffer_5_out), .Q(BP_q), .clr(Reset));
  Counter #(.max('hffff), .width(16)) counter_1 (
    .clr(Reset), .load(SP1), .up(WRT_t), .count(PSHPOP), .clk(controlled_buffer_5_out),
    .D(controlled_buffer_7_out), .Q(counter_1_q));  // open: carry
  Buffering buffering_3 (.in_1(CLOCK1), .out_2(buffering_3_out_2));
  assign controlled_buffer_11_out = MOV ? OP : 16'bz;  // Controlled_Buffer controlled_buffer_11
  assign controlled_buffer_11_out = AMD ? and_1_out : 16'bz;  // Controlled_Buffer controlled_buffer_12
  assign controlled_buffer_11_out = OW ? or_1_out : 16'bz;  // Controlled_Buffer controlled_buffer_13
  assign controlled_buffer_11_out = XOW ? xor_2_out : 16'bz;  // Controlled_Buffer controlled_buffer_14
  assign controlled_buffer_11_out = ADD ? adder_1_out : 16'bz;  // Controlled_Buffer controlled_buffer_15
  assign controlled_buffer_11_out = SUB ? subtractor_2_out : 16'bz;  // Controlled_Buffer controlled_buffer_16
  assign OP = A3 ? register_1_q : 16'bz;  // Controlled_Buffer controlled_buffer_17
  assign controlled_buffer_18_out = A2 ? register_1_q : 16'bz;  // Controlled_Buffer controlled_buffer_18
  assign OP = B3 ? register_2_q : 16'bz;  // Controlled_Buffer controlled_buffer_19
  assign controlled_buffer_18_out = B2 ? register_2_q : 16'bz;  // Controlled_Buffer controlled_buffer_20
  assign OP = C3 ? register_3_q : 16'bz;  // Controlled_Buffer controlled_buffer_21
  assign controlled_buffer_18_out = C2 ? register_3_q : 16'bz;  // Controlled_Buffer controlled_buffer_22
  assign OP = D3 ? register_4_q : 16'bz;  // Controlled_Buffer controlled_buffer_23
  assign controlled_buffer_18_out = D2 ? register_4_q : 16'bz;  // Controlled_Buffer controlled_buffer_24
  assign OP = s3 ? register_5_q : 16'bz;  // Controlled_Buffer controlled_buffer_25
  assign controlled_buffer_18_out = s2 ? register_5_q : 16'bz;  // Controlled_Buffer controlled_buffer_26
  assign OP = t3 ? register_6_q : 16'bz;  // Controlled_Buffer controlled_buffer_27
  assign controlled_buffer_18_out = t2 ? register_6_q : 16'bz;  // Controlled_Buffer controlled_buffer_28
  assign OP = BP3 ? BP_q : 16'bz;  // Controlled_Buffer controlled_buffer_29
  assign controlled_buffer_18_out = BP2 ? BP_q : 16'bz;  // Controlled_Buffer controlled_buffer_30
  assign and_1_out = OP & controlled_buffer_18_out;  // AND_Gate and_1, 16 bits wide
  assign or_1_out = OP | controlled_buffer_18_out;  // OR_Gate or_1, 16 bits wide
  assign xor_2_out = OP ^ controlled_buffer_18_out;  // XOR_Gate xor_2, 16 bits wide
  assign OP = SP3 ? counter_1_q : 16'bz;  // Controlled_Buffer controlled_buffer_31
  assign controlled_buffer_18_out = SP2 ? counter_1_q : 16'bz;  // Controlled_Buffer controlled_buffer_32
  Buffering buffering_4 (.in_1(buffering_3_out_2), .out_2(CLOCK2));
  REG_Decoder reg_decoder_1 (
    .IP(controlled_buffer_3_out[3:1]), .ENABLE(cpu_decoder_1_ou), .A(A1), .B(B1), .C(C1), .D(D1), .s(s1),
    .t(t1), .BP(BP1), .SP(SP1));
  REG_Decoder reg_decoder_2 (
    .IP(controlled_buffer_3_out[6:4]), .ENABLE(cpu_decoder_1_src_2), .A(A2), .B(B2), .C(C2), .D(D2), .s(s2),
    .t(t2), .BP(BP2), .SP(SP2));
  REG_Decoder reg_decoder_3 (
    .IP(controlled_buffer_3_out[9:7]), .ENABLE(controlled_buffer_8_out), .A(A3), .B(B3), .C(C3), .D(D3),
    .s(s3), .t(t3), .BP(BP3), .SP(SP3));
  Subtractor #(.width(16)) subtractor_1 (
    .a(counter_1_q), .b({16{1'b0}}), .out(subtractor_1_out), .bin(POP));  // open: bout
  Adder #(.width(16)) adder_1 (.a(OP), .b(controlled_buffer_18_out), .out(adder_1_out));  // open: cin, cout
  Subtractor #(.width(16)) subtractor_2 (
    .a(OP), .b(controlled_buffer_18_out), .out(subtractor_2_out));  // open: bin, bout
  not not_6 (not_6_out, PSHPOP);
  assign ADDR = PSHPOP ? subtractor_1_out : 16'bz;  // Controlled_Buffer controlled_buffer_33
  and and_2 (PUSH, WRT_t, INV_VAL);
  and and_3 (POP, READ, INV_VAL);
  assign ADDR = not_6_out ? controlled_buffer_18_out : 16'bz;  // Controlled_Buffer controlled_buffer_34
  Comparator #(.mode("unsigned"), .width(16)) comparator_1 (
    .a(OP), .b(controlled_buffer_18_out), .gt(comparator_1_gt[0]), .eq(comparator_1_gt[1]),
    .lt(comparator_1_gt[2]));
  or or_2 (PSHPOP, PUSH, POP);
  Register #(.width(3)) register_7 (
    .D(comparator_1_gt), .en(CMP), .clk(controlled_buffer_5_out), .Q(register_7_q), .clr(Reset));
  assign controlled_buffer_35_out = not_7_out ? register_7_q : 3'bz;  // Controlled_Buffer controlled_buffer_35
  not not_7 (not_7_out, INV_VAL);
  assign controlled_buffer_35_out = INV_VAL ? ~register_7_q : 3'bz;  // Controlled_Inverter controlled_inverter_2
  and and_4 (and_4_out, JL, controlled_buffer_35_out[0]);
  and and_5 (and_5_out, JE, controlled_buffer_35_out[1]);
  and and_6 (and_6_out, JG, controlled_buffer_35_out[2]);
  or or_3 (or_3_out, and_6_out, and_5_out, and_4_out, and_7_out);
  buf buffer_7 (buffer_7_out, CLOCK3);
  buf buffer_8 (buffer_8_out, buffer_7_out);
  buf buffer_9 (Clock_OU, buffer_8_out);
  buf and_7 (and_7_out, JMP);  // AND_Gate
  Counter #(.max('hffff), .width(16)) counter_2 (
    .clr(Reset), .load(or_3_out), .clk(controlled_buffer_5_out), .D(OP), .Q(Instruction_Pointer));  // open: up, count, carry
  and and_8 (WRT, WRT_t, CLOCK3);

  // Other names for the same wires on the sheet: CLOCK0 = Clock; INS[15:0] = OP
endmodule

module CPU_Decoder (
  input  [3:0] OPCODE,
  input  UNENABLE,
  output NOOP,
  output MOV,
  output AMD,
  output OW,
  output XOW,
  output ADD,
  output SUB,
  output SHL,
  output SHR,
  output CMP,
  output JMP,
  output JE,
  output JL,
  output JG,
  output WRT,
  output READ,
  output SRC_1,
  output SRC_2,
  output OU
);

  wire not_1_out;
  wire [3:0] and_1_out, controlled_buffer_1_out;

  assign controlled_buffer_1_out = not_1_out ? 4'b1111 : 4'bz;  // Controlled_Buffer controlled_buffer_1
  not not_1 (not_1_out, UNENABLE);
  assign and_1_out = OPCODE & controlled_buffer_1_out;  // AND_Gate and_1, 4 bits wide
  assign controlled_buffer_1_out = UNENABLE ? ~4'b1111 : 4'bz;  // Controlled_Inverter controlled_inverter_1
  Decoder #(.enable("false"), .select(4)) decoder_1 (
    .out0(NOOP), .out1(MOV), .out2(AMD), .out3(OW), .out4(XOW), .out5(ADD), .out6(SUB), .out7(SHL),
    .out8(SHR), .out9(CMP), .out10(JMP), .out11(JE), .out12(JL), .out13(JG), .out14(WRT), .out15(READ),
    .sel(and_1_out));
  nor nor_1 (OU, NOOP, CMP, JMP, JE, JL, JG, WRT);
  nor nor_2 (SRC_1, NOOP, READ, UNENABLE);
  or or_1 (SRC_2, AMD, OW, XOW, WRT, ADD, SUB, CMP, READ);
endmodule

module REG_Decoder (
  input  [2:0] IP,
  input  ENABLE,
  output A,
  output B,
  output C,
  output D,
  output s,
  output t,
  output BP,
  output SP
);

  Demultiplexer #(.select(3)) demultiplexer_1 (
    .out0(A), .out1(B), .out2(C), .out3(D), .out4(s), .out5(t), .out6(BP), .out7(SP), .in(ENABLE), .sel(IP));
endmodule

module INSTR_SAVE (
  input  [15:0] IP,
  input  WE,
  input  Clock,
  input  Reset,
  output [15:0] out_5
);

  Register #(.trigger("falling"), .width(16)) register_1 (
    .D({1'b0, IP[14:0]}), .en(WE), .clk(Clock), .Q(out_5), .clr(Reset));
endmodule

module Buffering (
  input  in_1,
  output out_2
);

  wire buffer_1_out, buffer_2_out, buffer_3_out, buffer_4_out, buffer_5_out, buffer_6_out, buffer_7_out,
       buffer_8_out, buffer_9_out;

  buf buffer_1 (buffer_1_out, in_1);
  buf buffer_2 (buffer_2_out, buffer_1_out);
  buf buffer_3 (buffer_3_out, buffer_2_out);
  buf buffer_4 (buffer_4_out, buffer_3_out);
  buf buffer_5 (buffer_5_out, buffer_4_out);
  buf buffer_6 (buffer_6_out, buffer_5_out);
  buf buffer_7 (buffer_7_out, buffer_6_out);
  buf buffer_8 (buffer_8_out, buffer_7_out);
  buf buffer_9 (buffer_9_out, buffer_8_out);
  buf buffer_10 (out_2, buffer_9_out);
endmodule

module IMM_SAVE (
  input  IMM_VAL,
  input  [15:0] INSTR_IN,
  input  Clock,
  input  Reset,
  output [15:0] out_5,
  output IMM_ENABLE
);

  wire and_1_out, not_1_out;

  and and_1 (and_1_out, not_1_out, IMM_VAL);
  not not_1 (not_1_out, IMM_ENABLE);
  D_Flip_Flop #(.trigger("falling")) d_ff_1 (
    .D(and_1_out), .clk(Clock), .Q(IMM_ENABLE), .reset(Reset));  // open: Qn, preset
  Register #(.width(16)) register_1 (.D(INSTR_IN), .en(and_1_out), .clk(Clock), .Q(out_5), .clr(Reset));

  // Other names for the same wires on the sheet: IMM_EN = IMM_ENABLE
endmodule
